# Fritzing sketch 4duino connections (saved by Fritzing 0.9.6b)
stripboards: 1

parts:
  J6 = male pin header, 4 pins [form="♂ (male)"]
  S1 = Toggle Switch [package=THT]
  J10 = Screw terminal - 2 pins [package=THT]
  J11 = male pin header, 3 pins [form="♂ (male)"]
  J12 = male pin header, 4 pins [form="♂ (male)"]
  J13 = male pin header, 4 pins [form="♂ (male)"]
  Part4 = Adafruit Proto Shield R3 [part_number="Adafruit #2077"]

nets:
  N1: J6.pin1, J11.pin1, J12.pin1, J13.pin4
  N2: J6.pin2, Part4.D11
  N3: J6.pin3, Part4.D12
  N4: J6.pin4, J12.pin4, J13.pin1
  N5: S1.L1, J10.pin1, Part4.1#166, Part4.P$5#167
  N6: S1.COM, J10.pin2, Part4.1#169, Part4.P$5#170, Part4.P$6
  N7: S1.L2, Part4.N$140
  N8: J11.pin2, Part4.SCL
  N9: J11.pin3, Part4.SDA
  N10: J12.pin2, Part4.D7
  N11: J12.pin3, Part4.D8
  N12: J13.pin2, Part4.D4
  N13: J13.pin3, Part4.D3

notes:
  pwr
  ws2801
  i2c
  enc1
  enc2
  5v
  gnd

custom parts:
  Adafruit Proto Shield R3: This prototyping shield is the best out there (well, we think so, at least), and now is even better with Version R3 - updated for the most compatibility with just about all the Arduinos! It works with UNO, Mega, Leonardo, NG, Diecimila, Duemilanove, and compatible Arduinos. Yun's and Arduino Ethernets have a chunky Ethernet jack that gets in the way of stacking, you can use the stacking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
