# Fritzing sketch perma-proto-RaspberryPi-layout (saved by Fritzing 0.9.6b)

parts:
  Part1 = Adafruit Perma-Proto HAT [part_number="Adafruit #2314 and #2310"]
  U1 = JST XH 3A Male [chip_label=? package=THT]
  U2 = JST XH 4A 2.54mm [package=THT]
  U3 = JST XH 4A 2.54mm [package=THT]
  U4 = JST XH 4A 2.54mm [package=THT]
  U5 = JST XH 4A 2.54mm [package=THT]

nets:
  N1: Part1.SDA, Part1.N$61#371
  N2: Part1.SCL, Part1.N$59#361
  N3: Part1.GPIO18, Part1.N$56#346
  N4: Part1.GPIO27, Part1.N$55#341
  N5: Part1.GPIO24, Part1.N$51#321
  N6: Part1.GPIO25, Part1.N$49#311
  N7: Part1.GPIO12, Part1.N$46#296
  N8: Part1.GPIO13, Part1.N$45#291
  N9: Part1.3.3V, Part1.N$47#301, Part1.N$52#326, Part1.N$57#351, Part1.N$62
  N10: Part1.5.0V, Part1.N$1#156
  N11: Part1.GND, Part1.N$4#171, Part1.N$44#286, Part1.N$50#316, Part1.N$53#331, Part1.N$60#366
  N12: Part1.N$1#159, U2.pin4
  N13: Part1.N$2#164, U2.pin3
  N14: Part1.N$2#165, Part1.N$61#375
  N15: Part1.N$3#169, U2.pin2
  N16: Part1.N$3#170, Part1.N$59#365
  N17: Part1.N$4#174, U2.pin1
  N18: Part1.N$44#289, U5.pin1
  N19: Part1.N$45#294, U5.pin2
  N20: Part1.N$46#299, U5.pin3
  N21: Part1.N$47#304, U5.pin4
  N22: Part1.N$49#314, U4.pin2
  N23: Part1.N$50#319, U4.pin1
  N24: Part1.N$51#324, U4.pin3
  N25: Part1.N$52#329, U4.pin4
  N26: Part1.N$53#334, U3.pin1
  N27: Part1.N$55#345, U3.pin2
  N28: Part1.N$56#349, U3.pin3
  N29: Part1.N$57#354, U3.pin4
  N30: Part1.N$59#364, U1.pin2
  N31: Part1.N$60#369, U1.pin1
  N32: Part1.N$61#374, U1.pin3

notes:
  4uino
  line sensor
  i2c

custom parts:
  Adafruit Perma-Proto HAT: To kick off the Adafruit HAT party, we have this Perma-Proto inspired plug in daughter board. It has a grid of 0.1" prototyping soldering holes for attaching chips, resistors, LED, potentiometers and more. The holes are connected underneath with traces to mimic the solderless breadboards you're familiar. There's also long power strips for +3V, +5V and Ground connections to the Pi. Near the top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
  JST XH 3A Male: 2.54 Mm JST "XH" connector
  JST XH 4A 2.54mm: 4 Pin JST XH connector
