# Fritzing sketch perma-proto-simple-electronics (saved by Fritzing 0.9.3b)
stripboards: 1

parts:
  Part1 = Adafruit Perma-Proto HAT [part_number="Adafruit #2314 and #2310"]
  J1 = male pin header, 4 pins [form="♂ (male)"]
  J2 = male pin header, 4 pins [form="♂ (male)"]
  J3 = male pin header, 4 pins [form="♂ (male)"]
  J4 = male pin header, 4 pins [form="♂ (male)"]
  J6 = male pin header, 4 pins [form="♂ (male)"]
  S1 = Toggle Switch [package=THT]
  J10 = Screw terminal - 2 pins [package=THT]
  J11 = male pin header, 3 pins [form="♂ (male)"]
  J12 = male pin header, 4 pins [form="♂ (male)"]
  J13 = male pin header, 4 pins [form="♂ (male)"]
  J14 = male pin header, 4 pins [form="♂ (male)"]
  J15 = male pin header, 4 pins [form="♂ (male)"]
  J16 = male pin header, 4 pins [form="♂ (male)"]
  Part4 = Adafruit Proto Shield R3 [part_number="Adafruit #2077"]

nets:
  N1: Part1.SDA, Part1.N$61#371
  N2: Part1.SCL, Part1.N$59#361
  N3: Part1.GPIO18, Part1.N$56#346
  N4: Part1.GPIO27, Part1.N$55#341
  N5: Part1.GPIO24, Part1.N$51#321
  N6: Part1.GPIO25, Part1.N$49#311
  N7: Part1.GPIO12, Part1.N$46#296
  N8: Part1.GPIO13, Part1.N$45#291
  N9: Part1.3.3V, Part1.N$47#301, Part1.N$52#326, Part1.N$57#351, Part1.N$62#376
  N10: Part1.5.0V, Part1.N$1#156
  N11: Part1.GND, Part1.N$4#171, Part1.N$44#286, Part1.N$50#316, Part1.N$53#331, Part1.N$60#366
  N12: Part1.N$1#157, J4.pin1
  N13: Part1.N$1#159, J3.pin1
  N14: Part1.N$2#162, J4.pin2
  N15: Part1.N$2#164, J3.pin2
  N16: Part1.N$2#165, Part1.N$61#375
  N17: Part1.N$3#167, J4.pin3
  N18: Part1.N$3#169, J3.pin3
  N19: Part1.N$3#170, Part1.N$59#365
  N20: Part1.N$4#172, J4.pin4
  N21: Part1.N$4#174, J3.pin4
  N22: Part1.N$44#289, J16.pin4
  N23: Part1.N$45#294, J16.pin3
  N24: Part1.N$46#299, J16.pin2
  N25: Part1.N$47#304, J16.pin1
  N26: Part1.N$49#314, J15.pin3
  N27: Part1.N$50#319, J15.pin4
  N28: Part1.N$51#324, J15.pin2
  N29: Part1.N$52#329, J15.pin1
  N30: Part1.N$53#334, J14.pin4
  N31: Part1.N$55#345, J14.pin3
  N32: Part1.N$56#349, J14.pin2
  N33: Part1.N$57#354, J14.pin1
  N34: Part1.N$59#362, J1.pin3
  N35: Part1.N$59#364, J2.pin3
  N36: Part1.N$60#367, J1.pin4
  N37: Part1.N$60#369, J2.pin4
  N38: Part1.N$61#372, J1.pin2
  N39: Part1.N$61#374, J2.pin2
  N40: Part1.N$62#377, J1.pin1
  N41: Part1.N$62#379, J2.pin1
  N42: J6.pin1, J11.pin1, J12.pin1, J13.pin4
  N43: J6.pin2, Part4.D11
  N44: J6.pin3, Part4.D12
  N45: J6.pin4, J12.pin4, J13.pin1
  N46: S1.L1, J10.pin1, Part4.1#166, Part4.P$5#167, Part4.P$6#168
  N47: S1.COM, J10.pin2, Part4.1#169, Part4.P$5#170, Part4.P$6#171
  N48: S1.L2, Part4.N$140
  N49: J11.pin2, Part4.SCL
  N50: J11.pin3, Part4.SDA
  N51: J12.pin2, Part4.D7
  N52: J12.pin3, Part4.D8
  N53: J13.pin2, Part4.D4
  N54: J13.pin3, Part4.D3

notes:
  4uino
  line sensor
  pwr
  ws2801
  i2c
  enc1
  enc2
  5v
  gnd

custom parts:
  Adafruit Perma-Proto HAT: To kick off the Adafruit HAT party, we have this Perma-Proto inspired plug in daughter board. It has a grid of 0.1" prototyping soldering holes for attaching chips, resistors, LED, potentiometers and more. The holes are connected underneath with traces to mimic the solderless breadboards you're familiar. There's also long power strips for +3V, +5V and Ground connections to the Pi. Near the top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
  Adafruit Proto Shield R3: This prototyping shield is the best out there (well, we think so, at least), and now is even better with Version R3 - updated for the most compatibility with just about all the Arduinos! It works with UNO, Mega, Leonardo, NG, Diecimila, Duemilanove, and compatible Arduinos. Yun's and Arduino Ethernets have a chunky Ethernet jack that gets in the way of stacking, you can use the stacking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
